// Logisim project task1.circ as structural Verilog: 1 circuit, main circuit main
module main (
  input  IN_CARRY,
  input  [3:0] IN_A,
  input  [3:0] IN_B,
  output [3:0] OUT_SUM
);

  wire and_1_out, and_2_out, and_3_out, and_4_out, buffer_1_out, buffer_2_out, buffer_3_out, buffer_4_out,
       buffer_5_out, buffer_6_out, odd_parity_1_out, odd_parity_2_out, odd_parity_3_out, odd_parity_4_out,
       or_1_out, or_2_out, or_3_out, or_4_out, or_5_out, or_6_out, or_7_out, or_8_out, or_9_out, or_10_out,
       or_11_out, or_12_out;

  xor odd_parity_1 (odd_parity_1_out, IN_CARRY, IN_A[0], IN_B[0]);
  or or_1 (or_1_out, IN_CARRY, IN_A[0]);
  or or_2 (or_2_out, IN_CARRY, IN_B[0]);
  and and_1 (and_1_out, or_1_out, or_2_out, or_3_out);
  or or_3 (or_3_out, IN_A[0], IN_B[0]);
  buf buffer_1 (buffer_1_out, IN_A[1]);
  buf buffer_2 (buffer_2_out, IN_B[1]);
  xor odd_parity_2 (odd_parity_2_out, and_1_out, buffer_1_out, buffer_2_out);
  or or_4 (or_4_out, and_1_out, buffer_1_out);
  or or_5 (or_5_out, and_1_out, buffer_2_out);
  or or_6 (or_6_out, buffer_1_out, buffer_2_out);
  and and_2 (and_2_out, or_4_out, or_5_out, or_6_out);
  buf buffer_3 (buffer_3_out, IN_A[2]);
  buf buffer_4 (buffer_4_out, IN_B[2]);
  xor odd_parity_3 (odd_parity_3_out, and_2_out, buffer_3_out, buffer_4_out);
  or or_7 (or_7_out, and_2_out, buffer_3_out);
  or or_8 (or_8_out, and_2_out, buffer_4_out);
  or or_9 (or_9_out, buffer_3_out, buffer_4_out);
  and and_3 (and_3_out, or_7_out, or_8_out, or_9_out);
  buf buffer_5 (buffer_5_out, IN_A[3]);
  buf buffer_6 (buffer_6_out, IN_B[3]);
  xor odd_parity_4 (odd_parity_4_out, and_3_out, buffer_5_out, buffer_6_out);
  or or_10 (or_10_out, and_3_out, buffer_5_out);
  or or_11 (or_11_out, and_3_out, buffer_6_out);
  or or_12 (or_12_out, buffer_5_out, buffer_6_out);
  buf OUT_0_BIT (OUT_SUM[0], odd_parity_1_out);
  buf OUT_1_BIT (OUT_SUM[1], odd_parity_2_out);
  buf OUT_2_BIT (OUT_SUM[2], odd_parity_3_out);
  buf OUT_3_BIT (OUT_SUM[3], odd_parity_4_out);
  and and_4 (and_4_out, or_10_out, or_11_out, or_12_out);
  // Probe on and_4_out
endmodule
