// Logisim project task2.circ as structural Verilog: 1 circuit, main circuit main
module main (
);

  wire and_1_out, and_2_out, and_3_out, and_4_out, and_5_out, and_6_out, and_7_out, and_8_out, and_9_out,
       clock_1_out, LOCK_out, nor_1_out, not_1_out, or_1_out, or_2_out, RST_out, s_r_ff_1_q, s_r_ff_2_q,
       s_r_ff_3_q, s_r_ff_3_qn, s_r_ff_4_q, s_r_ff_5_q, shift_register_1_q0, shift_register_1_q1,
       shift_register_1_q2, UNLOCK_out;

  Clock clock_1 (.out(clock_1_out));
  and and_1 (and_1_out, not_1_out, and_3_out);
  and and_2 (and_2_out, and_8_out, s_r_ff_3_qn);
  S_R_Flip_Flop s_r_ff_1 (
    .S(and_1_out), .clk(clock_1_out), .R(and_2_out), .Q(s_r_ff_1_q), .reset(RST_out));  // open: Qn, preset, en
  and and_3 (and_3_out, UNLOCK_out, s_r_ff_4_q);
  Button RST (.out(RST_out));
  and and_4 (and_4_out, UNLOCK_out, s_r_ff_4_q);
  Button LOCK (.out(LOCK_out));
  and and_5 (and_5_out, LOCK_out, s_r_ff_2_q);
  S_R_Flip_Flop s_r_ff_2 (
    .S(and_8_out), .clk(clock_1_out), .R(shift_register_1_q0), .Q(s_r_ff_2_q), .preset(RST_out));  // open: Qn, reset, en
  and and_6 (and_6_out, shift_register_1_q1, not_1_out);
  Button UNLOCK (.out(UNLOCK_out));
  S_R_Flip_Flop s_r_ff_3 (
    .S(and_5_out), .clk(clock_1_out), .R(and_4_out), .Q(s_r_ff_3_q), .Qn(s_r_ff_3_qn), .reset(RST_out));  // open: preset, en
  and and_7 (and_7_out, s_r_ff_3_q, s_r_ff_2_q);
  or or_1 (or_1_out, s_r_ff_1_q, s_r_ff_5_q);
  Shift_Register #(.length(3)) shift_register_1 (
    .clk(clock_1_out), .load(clock_1_out), .clr(RST_out), .d0(and_7_out), .q0(shift_register_1_q0),
    .d1(or_1_out), .q1(shift_register_1_q1), .d2(s_r_ff_4_q), .q2(shift_register_1_q2));  // open: shift, in, out
  S_R_Flip_Flop s_r_ff_4 (
    .S(and_6_out), .clk(clock_1_out), .R(and_8_out), .Q(s_r_ff_4_q), .reset(RST_out));  // open: Qn, preset, en
  nor nor_1 (nor_1_out, shift_register_1_q1, shift_register_1_q2);
  and and_8 (and_8_out, shift_register_1_q1, shift_register_1_q2);
  not not_1 (not_1_out, and_8_out);
  and and_9 (and_9_out, s_r_ff_2_q, nor_1_out);
  LED led_1 (.in(shift_register_1_q2));
  S_R_Flip_Flop s_r_ff_5 (
    .S(shift_register_1_q0), .clk(clock_1_out), .R(shift_register_1_q1), .Q(s_r_ff_5_q), .reset(RST_out));  // open: Qn, preset, en
  LED led_2 (.in(shift_register_1_q1));
  LED led_3 (.in(or_2_out));
  or or_2 (or_2_out, and_9_out, shift_register_1_q0);
endmodule
